# Fritzing sketch Sketch Omnitrix rec (saved by Fritzing 0.9.3b)
breadboards: 1

parts:
  RE1 = KY-040 Rotary encoder [package=THT]
  R1 = Resistor [tolerance=±5% resistance=10k package=THT]
  S1 = Pushbutton [package="[THT]"]
  A1 = Wemos S2 Mini [part_number="WeMos D1 Mini Lite"]
  LCD1 = Waveshare 1.28 inch Round 240x240 LCD Display

nets:
  N1: RE1.GND, R1.Pin_1, A1.Pin_18, A1.Pin_26, LCD1.pin2
  N2: RE1.Vcc, S1.Pin_3, S1.Pin_4, A1.Pin_8, LCD1.pin_1
  N3: RE1.SW, A1.Pin_4
  N4: RE1.DT, A1.Pin_32
  N5: RE1.CLK, A1.Pin_24
  N6: R1.Pin_0, S1.Pin_1, S1.Pin_2, A1.Pin_27
  N7: A1.Pin_10, LCD1.pin_6
  N8: A1.Pin_11, LCD1.pin_7
  N9: A1.Pin_14, LCD1.pin_5
  N10: A1.Pin_21, LCD1.pin3
  N11: A1.Pin_22, LCD1.pin4

custom parts:
  KY-040 Rotary encoder: KY-040 Rotary Encoder with switch on breakout borad from AZ Delivery
  Wemos S2 Mini: A mini wifi board based on the ESP32-S2FN4R2.
  Waveshare 1.28 inch Round 240x240 LCD Display: Waveshare 1.28 inch Round 240x240 LCD Display with GC9A01 Controller
