# Fritzing sketch Sketch Omnitrix (saved by Fritzing 0.9.3b)
breadboards: 1

parts:
  U1 = ESP32S-HiLetgo [part_number=ESP32S-HiLetgo]
  RE1 = KY-040 Rotary encoder [package=THT]
  R1 = Resistor [tolerance=±5% resistance=10k package=THT]
  S1 = Pushbutton [package="[THT]"]
  LCD1 = Waveshare 1.28 inch Round 240x240 LCD Display

nets:
  N1: U1.3.3, S1.Pin_3, S1.Pin_4
  N2: U1.GPIO40, RE1.SW
  N3: U1.GPIO39, RE1.DT
  N4: U1.GPIO35, LCD1.pin4
  N5: U1.GPIO33, LCD1.pin3
  N6: U1.GND, R1.Pin_1
  N7: U1.GPIO10, LCD1.pin_5
  N8: U1.GPIO7, RE1.CLK
  N9: U1.GPIO2, LCD1.pin_6
  N10: U1.GPIO4, LCD1.pin_7
  N11: U1.GPIO17, R1.Pin_0, S1.Pin_1, S1.Pin_2
  N12: RE1.GND, LCD1.pin2
  N13: RE1.Vcc, LCD1.pin_1

custom parts:
  ESP32S-HiLetgo: HiLetgo ESP-WROOM-32 ESP32 ESP-32S Development Board 2.4GHz Dual-Mode WiFi + Bluetooth Dual Cores Microcontroller The ESP32 integrated with Antenna switches, RF Balun, power amplifiers, low-noise amplifiers, filters, and management modules, and the entire solution occupies the least area of PCB. 2.4 GHz Wi-Fi plus Bluetooth dual-mode chip, with TSMC Ultra-low power consumption 40nm technology,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
  KY-040 Rotary encoder: KY-040 Rotary Encoder with switch on breakout borad from AZ Delivery
  Waveshare 1.28 inch Round 240x240 LCD Display: Waveshare 1.28 inch Round 240x240 LCD Display with GC9A01 Controller
